# Fritzing sketch Temp_Sensor (saved by Fritzing 0.9.3b)
breadboards: 1

parts:
  U1 = POT [package=pot_alpha_rv16af-20]
  R2 = Resistor [tolerance=±5% resistance=220 package="0603 [SMD]"]
  LCD2 = LCD screen
  Part2 = Adafruit Metro Mini [part_number="Adafruit #2590"]
  Part3 = Adafruit WINC1500 (uFL Antenna) Breakout [part_number="Adafruit #3060"]  # not connected
  DS7 = DS18B20 1-Wire Temperature Sensor Probe Cable
  DS8 = DS18B20 1-Wire Temperature Sensor Probe Cable
  U2 = POT [package=pot_alpha_rv16af-20]
  U3 = POT [package=pot_alpha_rv16af-20]

nets:
  VDD: U1.A, R2.Pin_0, LCD2.VDD, LCD2.LED+, Part2.+5V, DS7.VDD, DS8.VDD, U2.A, U3.A
  N1: U1.S, LCD2.V0
  GND: U1.E, LCD2.VSS, LCD2.R/W, LCD2.LED-, Part2.GND, DS7.GND, DS8.GND, U2.E, U3.E
  N2: LCD2.RS, Part2.IO12
  N3: LCD2.E, Part2.IO11
  N4: LCD2.DB4, Part2.IO10
  N5: LCD2.DB5, Part2.IO9
  N6: LCD2.DB6, Part2.IO8
  N7: LCD2.DB7, Part2.IO7
  N8: Part2.AD1, U3.S
  N9: Part2.AD0, U2.S
  N10: Part2.IO13, DS7.DQ, DS8.DQ

custom parts:
  Adafruit Metro Mini: We sure love the ATmega328 here at Adafruit, and we use them a lot for our own projects. The processor has plenty of GPIO, Analog inputs, hardware UART SPI and I2C, timers and PWM galore - just enough for most simple projects. When we need to go small, we use a Pro Trinket 3V or 5V, but if you want to have USB-to-Serial built in, we reach for an Adafruit METRO Mini. METRO Mini is the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
  Adafruit WINC1500 (uFL Antenna) Breakout: Connect your Arduino to the Internet with this fine new FCC-certified WiFi module from Atmel. This 802.11bgn-capable WiFi module is the best new thing for networking your devices, with SSL support and rock solid performance - running our adafruit.io MQTT demo for a full weekend straight with no hiccups (it would have run longer but we had to go to work, so we unplugged it). We like these so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
